# Fritzing sketch CNC Sketch-It Plotter (saved by Fritzing 0.9.3b)

parts:
  Part1 = Arduino Uno (Rev3) - ICSP
  M1 = DC Motor
  Pololu_A1 = Pololu A4988 [package=SO16]
  M4 = Stepper Motor - Unipolar
  Pololu_A3 = Pololu A4988 [package=SO16]
  C1 = Capacitor Polarized [package=panasonic_e]
  C2 = Capacitor Polarized [package=panasonic_e]
  M2 = Stepper Motor - Unipolar
  VCC1 = Battery block 9V
  VCC2 = Battery block 9V

nets:
  N1: Part1.D8, Pololu_A1.STEP
  N2: Part1.D9_PWM, Pololu_A1.DIR
  N3: Part1.D3_PWM, M1.pin_2
  N4: Part1.D4, M1.pin_1
  N5: Part1.D6_PWM, Pololu_A3.STEP
  N6: Part1.D7, Pololu_A3.DIR
  VDD: Part1.5V, Pololu_A1.VDD, Pololu_A3.VDD
  N7: Part1.GND, Pololu_A1.GND#8, Pololu_A3.GND#8
  N8: Pololu_A1.RESET, Pololu_A1.SLEEP
  N9: Pololu_A1.1B, M2.B
  N10: Pololu_A1.1A, M2.C
  N11: Pololu_A1.2A, M2.COMMON_1
  N12: Pololu_A1.2B, M2.A
  N13: Pololu_A1.GND#14, C1.+, VCC2.-
  N14: Pololu_A1.VMOT, C1.-, VCC2.+
  N15: M4.A, Pololu_A3.2B
  N16: M4.COMMON_1, Pololu_A3.2A
  N17: M4.C, Pololu_A3.1A
  N18: M4.B, Pololu_A3.1B
  N19: Pololu_A3.GND#14, C2.+, VCC1.-
  N20: Pololu_A3.VMOT, C2.-, VCC1.+
